# Fritzing sketch SKETCH PURIFICADOR (saved by Fritzing 0.9.3b)
breadboards: 1

parts:
  IC1 = MQ-2 [package="DIP (Dual Inline) [THT]"]
  Componente1 = Arduino Uno (Rev3)
  KY-6 = Keyes Relay [package=THT]
  Componente2 = Lilypad Battery Connect
  LED1 = LEDs [package=led10mm]

nets:
  N1: IC1.pin1, Componente1.5V, KY-6.power
  N2: IC1.pin2, Componente1.GND, KY-6.signal
  N3: IC1.pin4, Componente1.A0
  N4: Componente1.D9_PWM, KY-6.ground
  N5: KY-6.C, LED1.A
  N6: KY-6.NO, Componente2.-
  N7: Componente2.+, LED1.C

notes:
  MQ-135
  110V
  Energia
  RELAY
  dispositivo 110v
  (purificador de ar)

custom parts:
  MQ-2: MQ-2 Gas Sensor module
  Keyes Relay: The Keyes 5V relay module is suitable for SCM development, home appliance control. It uses a 5V~12V TIL control signal which can control DC / AC signal.
  LEDs: LEDs Standard schematic elements and footprints for 5mm, 3mm, 1206, and 0603 sized LEDs. 5mm - Spark Fun Electronics SKU : COM-00529 (and others)
